# Fritzing sketch motor driver (saved by Fritzing 0.9.10b)
breadboards: 1

parts:
  Composant1 = Arduino Nano (Rev3.0)
  C1 = Electrolytic Capacitor [capacitance=1µF voltage=35V package="100 mil [THT, electrolytic]"]
  J1_12_V = Power Jack [package=power_jack_combo]
  R1 = Rotary Potentiometer (Small) [maximum_resistance=100kΩ knob_status=50% power=0.5W package=THT]
  U1 = SWITCH_SPDT [package=kps-1290]
  R2 = Resistor [tolerance=±5% resistance=10k package="0402 [SMD]"]

nets:
  GND: Composant1.GND, C1.-, J1_12_V.GND, R1.leg2, U1.S
  N1: Composant1.VIN, C1.+, J1_12_V.PWR
  N2: Composant1.5V, R1.leg1, U1.O, R2.Pin_0
  N3: Composant1.A3, R1.wiper
  N4: Composant1.A1, U1.P, R2.Pin_1
